# Fritzing sketch Gateway (saved by Fritzing 0.9.2b)

parts:
  Arduino_UNO_+_Ethernet_W5100 = Arduino Uno (Rev3)
  NRF24 = NRF24L01
  PIR = PIR sensor
  MQ-2 = GAS_SENSOR [package=mq-3]
  2_channel_Relay_module = 2-Channel 5v Relay Shield [package=relay-2ch5v10a]
  5V_1A = Power plug
  C1 = Electrolytic Capacitor [capacitance=100μF package="0807 [SMD, electrolytic]"]  # not connected
  C3 = Electrolytic Capacitor [capacitance=100μF package="0807 [SMD, electrolytic]"]  # not connected
  C2 = Ceramic Capacitor [capacitance=470nF package="100 mil [THT, multilayer]"]  # not connected

nets:
  N1: Arduino_UNO_+_Ethernet_W5100.A0, NRF24.SCK
  N2: Arduino_UNO_+_Ethernet_W5100.A1, NRF24.MOSI
  N3: Arduino_UNO_+_Ethernet_W5100.A2, NRF24.MISO
  N4: Arduino_UNO_+_Ethernet_W5100.A5/SCL, MQ-2.B1
  N5: Arduino_UNO_+_Ethernet_W5100.D8, 2_channel_Relay_module.IN2
  N6: Arduino_UNO_+_Ethernet_W5100.D2, PIR.SIG
  N7: Arduino_UNO_+_Ethernet_W5100.D5_PWM, NRF24.CE
  N8: Arduino_UNO_+_Ethernet_W5100.D6_PWM, NRF24.CSN
  N9: Arduino_UNO_+_Ethernet_W5100.D7, 2_channel_Relay_module.IN1
  3V3: Arduino_UNO_+_Ethernet_W5100.3V3, NRF24.VCC
  VCC: Arduino_UNO_+_Ethernet_W5100.5V, MQ-2.H1, 2_channel_Relay_module.VCC, 5V_1A.VCC
  GND: Arduino_UNO_+_Ethernet_W5100.GND, NRF24.GND, PIR.GND, MQ-2.H2, 5V_1A.GND

custom parts:
  NRF24L01: NRF24L01 module
  2-Channel 5v Relay Shield: 2 Channel 5v Relay Shield w. 2x SPD-06VDC-SD-C
