# Fritzing sketch Hand-sensor (saved by Fritzing 0.9.2b)

parts:
  NRF24 = NRF24L01
  C3 = Electrolytic Capacitor [capacitance=100μF package="0807 [SMD, electrolytic]"]  # not connected
  C4 = Ceramic Capacitor [capacitance=220nF package="100 mil [THT, multilayer]"]  # not connected
  Part1 = Arduino Nano (Rev3.0)
  5V_0_5A = Power plug
  C1 = Electrolytic Capacitor [capacitance=100μF package="0807 [SMD, electrolytic]"]  # not connected
  C2 = Ceramic Capacitor [capacitance=100nF package="100 mil [THT, multilayer]"]  # not connected
  HC-SR04 = SRF05 Ultrasonic Rangefinder

nets:
  VCC: NRF24.VCC, Part1.3V3
  N1: NRF24.CSN, Part1.D10
  N2: NRF24.MOSI, Part1.D11/MOSI
  N3: NRF24.CE, Part1.D9
  N4: NRF24.SCK, Part1.D13/SCK
  N5: NRF24.MISO, Part1.D12/MISO
  N6: Part1.D7, Part1.D8, HC-SR04.Trig, HC-SR04.Echo
  5V: Part1.5V, 5V_0_5A.VCC

custom parts:
  NRF24L01: NRF24L01 module
