# Fritzing sketch Node (saved by Fritzing 0.9.2b)

parts:
  NRF24 = NRF24L01
  C3 = Electrolytic Capacitor [capacitance=100μF package="0807 [SMD, electrolytic]"]  # not connected
  C4 = Ceramic Capacitor [capacitance=470nF package="100 mil [THT, multilayer]"]  # not connected
  Part1 = Arduino Nano (Rev3.0)
  Buzzer = Piezo Speaker
  Water_leak = FC-28 Soil Hygrometer Module
  Part3 = FC-28 Soil Hygrometer Module - Probe
  Grove1 = Grove Infrared Receiver
  Grove2 = Grove Infrared Emitter
  MQ-2 = GAS_SENSOR [package=mq-3]
  DS1 = DS18B20 1-Wire Temperature Sensor [part_number=DS18B20]  # not connected
  5V_1_5A = Power plug
  R2 = Resistor [tolerance=±5% resistance=4.7k package="2010 [SMD]"]
  PIR1 = PIR sensor
  DHT22 = Humidity and Temperature Sensor RHT03
  C1 = Electrolytic Capacitor [capacitance=100μF package="0807 [SMD, electrolytic]"]  # not connected
  C2 = Ceramic Capacitor [capacitance=470nF package="100 mil [THT, multilayer]"]  # not connected
  4-Channel_Relay_module = 2-Channel 5v Relay Shield [package=relay-2ch5v10a]
  DSx = DS18B20 1-Wire Temperature Sensor [part_number=DS18B20]  # not connected
  DS3 = DS18B20 1-Wire Temperature Sensor [part_number=DS18B20]
  U2 = 2-Channel 5v Relay Shield [package=relay-2ch5v10a]
  C5 = Electrolytic Capacitor [capacitance=100μF package="0807 [SMD, electrolytic]"]

nets:
  VCC: NRF24.VCC, Part1.3V3
  N1: NRF24.CSN, Part1.D10
  N2: NRF24.MOSI, Part1.D11/MOSI
  N3: NRF24.CE, Part1.D9
  N4: NRF24.SCK, Part1.D13/SCK
  N5: NRF24.MISO, Part1.D12/MISO
  N6: Part1.D2, Grove1.RX
  N7: Part1.D3, Grove2.TX
  N8: Part1.D4, U2.IN2
  N9: Part1.D5, Buzzer.pin2
  N10: Part1.D6, U2.IN1
  N11: Part1.D7, 4-Channel_Relay_module.IN2
  N12: Part1.D8, 4-Channel_Relay_module.IN1
  N13: Part1.A7, MQ-2.B1
  N14: Part1.A3, DHT22.Data-signal
  N15: Part1.A2, PIR1.SIG
  N16: Part1.A1, DS3.DQ
  N17: Part1.A0, Water_leak.DO
  VCC_2: Water_leak.VCC, 5V_1_5A.VCC
  GND: Water_leak.GND, 5V_1_5A.GND
  N18: Water_leak.POS, Part3.POS
  N19: Water_leak.NEG, Part3.NEG
  N20: R2.Pin_1, DS3.VDD
  N21: 4-Channel_Relay_module.VCC, C5.+

custom parts:
  NRF24L01: NRF24L01 module
  FC-28 Soil Hygrometer Module: The FC-28 is a soil hygrometer module that uses the Texas Instruments LM393 comparator chip to provide an analog measurement of soil humidity. The digital output is high when soil moisture is over a certain threshold, as determined by adjusting the potentiometer.
  FC-28 Soil Hygrometer Module - Probe: The FC-28 is a soil hygrometer module that uses the Texas Instruments LM393 comparator chip to provide an analog measurement of soil humidity.
  2-Channel 5v Relay Shield: 2 Channel 5v Relay Shield w. 2x SPD-06VDC-SD-C
