# Fritzing sketch Power_220_wire (saved by Fritzing 0.9.2b)
breadboards: 1

parts:
  Socket1 = Header 2 [package=molex-1x2_lock]
  Main_Node_Box = 2-Channel 5v Relay Shield [package=relay-2ch5v10a]
  U2 = 2-Channel 5v Relay Shield [package=relay-2ch5v10a]
  Socket2 = Header 2 [package=molex-1x2_lock]
  Socket3 = Header 2 [package=molex-1x2_lock]
  Socket4 = Header 2 [package=molex-1x2_lock]
  Power_Plug_220V = Header 2 [package=molex-1x2_lock]
  Power_supply = Transformer [package=transformer]
  5V = Power plug

nets:
  N1: Socket1.1, Socket2.1, Socket3.1, Socket4.1, Power_Plug_220V.1, Power_supply.3
  N2: Socket1.2, Main_Node_Box.K2-On
  N3: Main_Node_Box.K1-On, Socket2.2
  N4: U2.K1-In, Power_Plug_220V.2
  N5: U2.K1-On, Socket4.2
  N6: U2.K2-On, Socket3.2
  N7: Power_supply.1, 5V.GND
  N8: Power_supply.4, 5V.VCC

custom parts:
  2-Channel 5v Relay Shield: 2 Channel 5v Relay Shield w. 2x SPD-06VDC-SD-C
